# Fritzing sketch DoorTransitionWiring (saved by Fritzing 0.9.3b)
breadboards: 1

parts:
  Part1 = Arduino Uno (Rev3)
  microSD1 = MicroSD Card Module
  R1 = Resistor [tolerance=±5% resistance=10k package=THT]
  R2 = Photocell (LDR) [package=THT]
  Part2 = Mono 2.5W Class D Audio Amplifier - PAM8302
  R3 = Resistor [tolerance=±5% resistance=220 package=THT]
  C1 = Ceramic Capacitor [capacitance=100nF package="100 mil [THT, multilayer]"]
  R5 = Rotary Potentiometer (Small) [maximum_resistance=100kΩ package=THT]
  R6 = Rotary Potentiometer (Small) [maximum_resistance=100kΩ package=THT]
  LED1 = LED - 5mm [color="Red (633nm)" package="5 mm [THT]"]
  S1 = SWITCH-MOMENTARY-2 [package=reed_switch_pth]
  S2 = Toggle Switch [package=THT]
  SP1 = SPEAKER [package=pcb_mount_speaker]

nets (from the schematic view):
  N1: Part1.A3, R6.wiper
  N2: Part1.A5/SCL, R1.Pin_1, R2.pin_0
  N3: Part1.D8, S1.2
  N4: Part1.D9_PWM, R3.Pin_0
  N5: Part1.D10_PWM/SS, microSD1.CS
  N6: Part1.D11_PWM/MOSI, microSD1.MOSI
  N7: Part1.D12/MISO, microSD1.MISO
  N8: Part1.D13/SCK, microSD1.SCK
  N9: Part1.D5_PWM, S2.COM
  N10: Part1.D6_PWM, Part2.SD
  N11: Part1.D7, LED1.anode
  VCC: Part1.5V, microSD1.VCC, R2.pin_1, Part2.VCC, R6.leg2
  GND: Part1.GND, microSD1.GND, R1.Pin_0, R3.Pin_1, C1.1, R5.leg1, R5.wiper, R6.leg1
  N12: Part2.GND, Part2.AIN-, C1.0, LED1.cathode, S1.1, S2.L1, S2.L2
  N13: Part2.AIN+, R5.leg2
  N14: Part2.VO+, SP1.-
  N15: Part2.VO-, SP1.+

custom parts:
  Mono 2.5W Class D Audio Amplifier - PAM8302: A super small but powerful mono amplifier able to deliver up to 2.5 Watts into 4-8 ohm impedance speakers. Inside the miniature chip is a class D controller, able to run from 2.0V-5.5VDC. Since the amp is a class D, its very efficient (over 90% efficient when driving an 8Ω speaker at over half a Watt) - making it perfect for portable and battery-powered projects.
